# Fritzing sketch Peppa Jump (saved by Fritzing 0.9.4)
breadboards: 1

parts:
  LCD1 = LCD screen
  R1 = Trimmer Potentiometer [maximum_resistance=10kΩ package=THT]
  HC-SR04_Sensor_1 = HC-SR04 Ultrasonic Distance Sensor
  Part1 = Arduino Uno (Rev3)

nets:
  VSS: LCD1.VSS, LCD1.R/W, LCD1.LED-, R1.leg1, HC-SR04_Sensor_1.GND
  VDD: LCD1.VDD, LCD1.LED+, R1.leg2, HC-SR04_Sensor_1.VCC
  N1: LCD1.V0, R1.wiper
  N2: LCD1.RS, Part1.D12/MISO
  N3: LCD1.E, Part1.D11_PWM/MOSI
  N4: LCD1.DB4, Part1.D5_PWM
  N5: LCD1.DB5, Part1.D4
  N6: LCD1.DB6, Part1.D3_PWM
  N7: LCD1.DB7, Part1.D2
  N8: HC-SR04_Sensor_1.TRIG, Part1.D10_PWM/SS
  N9: HC-SR04_Sensor_1.ECHO, Part1.D9_PWM
